# Fritzing sketch Arduino_calculator (saved by Fritzing 0.9.3b)
breadboards: 1

parts:
  OLED_I2C1 = OLED 128x64 I2C Monochrome Display
  Part1 = Arduino Nano (Rev3.0)
  Keypad4x1 = Keypad Membran 4x4

nets:
  N1: OLED_I2C1.SCK, Part1.D4
  GND: OLED_I2C1.GND, Part1.GND
  N2: Part1.A4, Keypad4x1.Pin3

custom parts:
  Keypad Membran 4x4: Membrane Keypad 4x4 Matrix
